// Logisim project 16 bit ALU.circ as structural Verilog: 3 circuits, main circuit ALU
module _1_bit_ALU (
  input  A,
  input  B,
  input  in_3,
  input  in_4,
  input  in_5,
  input  [4:0] in_6,
  output out_7,
  output Subout,
  output out_9
);

  wire and_1_out, multiplexer_1_out, multiplexer_2_out, not_1_out, not_2_out, or_1_out, xor_1_out;

  not not_1 (not_1_out, A);
  not not_2 (not_2_out, B);
  Multiplexer #(.enable("false")) multiplexer_1 (.in0(A), .in1(not_1_out), .out(multiplexer_1_out), .sel(in_6[4]));
  Multiplexer #(.enable("false")) multiplexer_2 (.in0(B), .in1(not_2_out), .out(multiplexer_2_out), .sel(in_6[3]));
  and and_1 (and_1_out, multiplexer_1_out, multiplexer_2_out);
  or or_1 (or_1_out, multiplexer_1_out, multiplexer_2_out);
  xor xor_1 (xor_1_out, multiplexer_1_out, multiplexer_2_out);
  Adder #(.width(1)) adder_1 (.a(multiplexer_1_out), .b(multiplexer_2_out), .out(Subout), .cin(in_5), .cout(out_9));
  Multiplexer #(.select(3), .enable("false")) multiplexer_3 (
    .in0(and_1_out), .in1(or_1_out), .in2(xor_1_out), .in3(Subout), .in4(in_3), .in5(in_4), .out(out_7),
    .sel(in_6[2:0]));  // open: in6, in7

  // Other names for the same wires on the sheet: ALU_1bit_op[2:0] = in_6[2:0]; Bnegate = in_6[3]; Ainvert = in_6[4]
endmodule

module _16_Bit_ALU_noShift (
  input  [15:0] in_1,
  input  [15:0] in_2,
  input  [4:0] in_3,
  output Zero,
  output out_5,
  output [15:0] out_6
);

  wire n1_bit_alu_1_out_9, n1_bit_alu_2_out_9, n1_bit_alu_3_out_9, n1_bit_alu_4_out_9, n1_bit_alu_5_out_9,
       n1_bit_alu_6_out_9, n1_bit_alu_7_out_9, n1_bit_alu_8_out_9, n1_bit_alu_9_out_9, n1_bit_alu_10_out_9,
       n1_bit_alu_11_out_9, n1_bit_alu_12_out_9, n1_bit_alu_13_out_9, n1_bit_alu_14_out_9,
       n1_bit_alu_15_out_9, n1_bit_alu_16_out_9, OverFlow, S15, Sltu;

  _1_bit_ALU u_1_bit_alu_1 (
    .A(in_1[0]), .B(in_2[0]), .out_7(out_6[0]), .in_6(in_3), .in_5(in_3[3]), .out_9(n1_bit_alu_1_out_9),
    .in_3(out_5), .in_4(Sltu));  // open: Subout
  _1_bit_ALU u_1_bit_alu_2 (
    .A(in_1[1]), .B(in_2[1]), .out_7(out_6[1]), .in_6(in_3), .in_5(n1_bit_alu_1_out_9),
    .out_9(n1_bit_alu_2_out_9), .in_3(1'b0), .in_4(1'b0));  // open: Subout
  _1_bit_ALU u_1_bit_alu_3 (
    .A(in_1[2]), .B(in_2[2]), .out_7(out_6[2]), .in_6(in_3), .in_5(n1_bit_alu_2_out_9),
    .out_9(n1_bit_alu_3_out_9), .in_3(1'b0), .in_4(1'b0));  // open: Subout
  _1_bit_ALU u_1_bit_alu_4 (
    .A(in_1[3]), .B(in_2[3]), .out_7(out_6[3]), .in_6(in_3), .in_5(n1_bit_alu_3_out_9),
    .out_9(n1_bit_alu_4_out_9), .in_3(1'b0), .in_4(1'b0));  // open: Subout
  _1_bit_ALU u_1_bit_alu_5 (
    .A(in_1[4]), .B(in_2[4]), .out_7(out_6[4]), .in_6(in_3), .in_5(n1_bit_alu_4_out_9),
    .out_9(n1_bit_alu_5_out_9), .in_3(1'b0), .in_4(1'b0));  // open: Subout
  _1_bit_ALU u_1_bit_alu_6 (
    .A(in_1[5]), .B(in_2[5]), .out_7(out_6[5]), .in_6(in_3), .in_5(n1_bit_alu_5_out_9),
    .out_9(n1_bit_alu_6_out_9), .in_3(1'b0), .in_4(1'b0));  // open: Subout
  _1_bit_ALU u_1_bit_alu_7 (
    .A(in_1[6]), .B(in_2[6]), .out_7(out_6[6]), .in_6(in_3), .in_5(n1_bit_alu_6_out_9),
    .out_9(n1_bit_alu_7_out_9), .in_3(1'b0), .in_4(1'b0));  // open: Subout
  _1_bit_ALU u_1_bit_alu_8 (
    .A(in_1[7]), .B(in_2[7]), .out_7(out_6[7]), .in_6(in_3), .in_5(n1_bit_alu_7_out_9),
    .out_9(n1_bit_alu_8_out_9), .in_3(1'b0), .in_4(1'b0));  // open: Subout
  _1_bit_ALU u_1_bit_alu_9 (
    .A(in_1[8]), .B(in_2[8]), .out_7(out_6[8]), .in_6(in_3), .in_5(n1_bit_alu_8_out_9),
    .out_9(n1_bit_alu_9_out_9), .in_3(1'b0), .in_4(1'b0));  // open: Subout
  _1_bit_ALU u_1_bit_alu_10 (
    .A(in_1[9]), .B(in_2[9]), .out_7(out_6[9]), .in_6(in_3), .in_5(n1_bit_alu_9_out_9),
    .out_9(n1_bit_alu_10_out_9), .in_3(1'b0), .in_4(1'b0));  // open: Subout
  _1_bit_ALU u_1_bit_alu_11 (
    .A(in_1[10]), .B(in_2[10]), .out_7(out_6[10]), .in_6(in_3), .in_5(n1_bit_alu_10_out_9),
    .out_9(n1_bit_alu_11_out_9), .in_3(1'b0), .in_4(1'b0));  // open: Subout
  _1_bit_ALU u_1_bit_alu_12 (
    .A(in_1[11]), .B(in_2[11]), .out_7(out_6[11]), .in_6(in_3), .in_5(n1_bit_alu_11_out_9),
    .out_9(n1_bit_alu_12_out_9), .in_3(1'b0), .in_4(1'b0));  // open: Subout
  _1_bit_ALU u_1_bit_alu_13 (
    .A(in_1[12]), .B(in_2[12]), .out_7(out_6[12]), .in_6(in_3), .in_5(n1_bit_alu_12_out_9),
    .out_9(n1_bit_alu_13_out_9), .in_3(1'b0), .in_4(1'b0));  // open: Subout
  _1_bit_ALU u_1_bit_alu_14 (
    .A(in_1[13]), .B(in_2[13]), .out_7(out_6[13]), .in_6(in_3), .in_5(n1_bit_alu_13_out_9),
    .out_9(n1_bit_alu_14_out_9), .in_3(1'b0), .in_4(1'b0));  // open: Subout
  _1_bit_ALU u_1_bit_alu_15 (
    .A(in_1[14]), .B(in_2[14]), .out_7(out_6[14]), .in_6(in_3), .in_5(n1_bit_alu_14_out_9),
    .out_9(n1_bit_alu_15_out_9), .in_3(1'b0), .in_4(1'b0));  // open: Subout
  _1_bit_ALU u_1_bit_alu_16 (
    .A(in_1[15]), .B(in_2[15]), .out_7(out_6[15]), .in_6(in_3), .in_5(n1_bit_alu_15_out_9),
    .out_9(n1_bit_alu_16_out_9), .in_3(1'b0), .in_4(1'b0), .Subout(S15));
  not not_1 (Sltu, n1_bit_alu_16_out_9);
  xor xor_1 (OverFlow, n1_bit_alu_15_out_9, n1_bit_alu_16_out_9);
  nor nor_1 (Zero, out_6[0], out_6[1], out_6[2], out_6[3], out_6[4], out_6[5], out_6[6], out_6[7], out_6[8], out_6[9], out_6[10], out_6[12], out_6[11], out_6[13], out_6[14], out_6[15]);
  xor xor_2 (out_5, OverFlow, S15);

  // Other names for the same wires on the sheet: A0 = in_1[0]; A1 = in_1[1]; A2 = in_1[2]; A3 = in_1[3]; A4 = in_1[4];
  //   A5 = in_1[5]; A6 = in_1[6]; A7 = in_1[7]; A8 = in_1[8]; A9 = in_1[9]; A10 = in_1[10]; A11 = in_1[11];
  //   A12 = in_1[12]; A13 = in_1[13]; A14 = in_1[14]; A15 = in_1[15]; B0 = in_2[0]; B1 = in_2[1]; B2 = in_2[2];
  //   B3 = in_2[3]; B4 = in_2[4]; B5 = in_2[5]; B6 = in_2[6]; B7 = in_2[7]; B8 = in_2[8]; B9 = in_2[9];
  //   B10 = in_2[10]; B11 = in_2[11]; B12 = in_2[12]; B13 = in_2[13]; B14 = in_2[14]; B15 = in_2[15]; O0 = out_6[0];
  //   O1 = out_6[1]; O2 = out_6[2]; O3 = out_6[3]; O4 = out_6[4]; O5 = out_6[5]; O6 = out_6[6]; O7 = out_6[7];
  //   O8 = out_6[8]; O9 = out_6[9]; O10 = out_6[10]; O11 = out_6[11]; O12 = out_6[12]; O13 = out_6[13];
  //   O14 = out_6[14]; O15 = out_6[15]; Selection[4:0] = in_3; Bnegate = in_3[3]; Slt = out_5

  // Notes on the sheet:
  //   Output
  //   A
  //   B
endmodule

module ALU (
  input  [15:0] in_1,
  input  [15:0] in_2,
  input  [7:0] in_3,
  output out_4,
  output out_5,
  output [15:0] out_6
);

  wire [3:0] bitselector_1_out;
  wire [15:0] multiplexer_1_out, n16_bit_alu_noshift_1_out_6, shifter_1_out, shifter_2_out, shifter_3_out,
       shifter_4_out;

  BitSelector #(.width(16), .group(4)) bitselector_1 (.in(in_2), .out(bitselector_1_out), .sel(2'b00));
  Shifter #(.width(16)) shifter_1 (.in(in_1), .\dist (bitselector_1_out), .out(shifter_1_out));
  Shifter #(.width(16), .shift("lr")) shifter_2 (.in(in_1), .\dist (bitselector_1_out), .out(shifter_2_out));
  Shifter #(.width(16), .shift("ar")) shifter_3 (.in(in_1), .\dist (bitselector_1_out), .out(shifter_3_out));
  Shifter #(.width(16), .shift("rr")) shifter_4 (.in(in_1), .\dist (bitselector_1_out), .out(shifter_4_out));
  _16_Bit_ALU_noShift u_16_bit_alu_noshift_1 (
    .in_1(in_1), .in_2(in_2), .out_6(n16_bit_alu_noshift_1_out_6), .in_3(in_3[7:3]), .Zero(out_5),
    .out_5(out_4));
  Multiplexer #(.select(2), .width(16), .enable("false")) multiplexer_1 (
    .in0(shifter_1_out), .in1(shifter_2_out), .in2(shifter_3_out), .in3(shifter_4_out),
    .out(multiplexer_1_out), .sel(in_3[1:0]));
  Multiplexer #(.width(16), .enable("false")) multiplexer_2 (
    .in0(n16_bit_alu_noshift_1_out_6), .in1(multiplexer_1_out), .out(out_6), .sel(in_3[2]));

  // Other names for the same wires on the sheet: ALU_without_shift_selection[4:0] = in_3[7:3]; Shift_flag = in_3[2];
  //   Shiftop_select[1:0] = in_3[1:0]

  // Notes on the sheet:
  //   A
  //   B
  //   ٍ
  //   Output
endmodule
