// Logisim project BTB6.circ as structural Verilog: 4 circuits, main circuit BTB
// Enable_PC
module BTB (
  input  [15:0] Recent_branch_adddress,
  input  Taken_or_not_taken,
  input  [15:0] Target_address,
  input  [2:0] _3_bit_index_Write,
  input  [2:0] _3_bit_index_Read,
  input  Enable_if_branch_jump,
  input  [15:0] Current_PC,
  input  CLK,
  output [15:0] Target_address_2,
  output Prediction,
  output Previous_Prediction
);

  wire clk_t, or_2_out, reg_file_2_1_prediction, write, write_2;
  wire [15:0] Read_adddress, subtractor_1_out, subtractor_2_out;

  not not_1 (clk_t, CLK);
  Subtractor #(.width(16)) subtractor_1 (
    .a(Recent_branch_adddress), .b(Read_adddress), .out(subtractor_1_out));  // open: bin, bout
  Subtractor #(.width(16)) subtractor_2 (.a(Read_adddress), .b(Current_PC), .out(subtractor_2_out));  // open: bin, bout
  or or_1 (write, subtractor_1_out[0], subtractor_1_out[1], subtractor_1_out[2], subtractor_1_out[3], subtractor_1_out[4], subtractor_1_out[5], subtractor_1_out[6], subtractor_1_out[7], subtractor_1_out[9], subtractor_1_out[10], subtractor_1_out[11], subtractor_1_out[12], subtractor_1_out[13], subtractor_1_out[14], subtractor_1_out[15], subtractor_1_out[8]);
  or or_2 (or_2_out, subtractor_2_out[0], subtractor_2_out[1], subtractor_2_out[2], subtractor_2_out[3], subtractor_2_out[4], subtractor_2_out[5], subtractor_2_out[6], subtractor_2_out[7], subtractor_2_out[9], subtractor_2_out[10], subtractor_2_out[11], subtractor_2_out[12], subtractor_2_out[13], subtractor_2_out[14], subtractor_2_out[15], subtractor_2_out[8]);
  not not_2 (write_2, or_2_out);
  reg_file reg_file_1 (
    .in_1(clk_t), .RW(_3_bit_index_Write), .reg_write(write), .Bus_A(Read_adddress),
    .BUS_W(Recent_branch_adddress), .RA(_3_bit_index_Read), .Enable(Enable_if_branch_jump));  // open: out_8, out_9, out_10, out_11, out_12, out_13, out_14, out_15
  reg_file_2 reg_file_2_1 (
    .in_1(clk_t), .RW(_3_bit_index_Write), .reg_write(write), .Enable(Enable_if_branch_jump),
    .Bus_A(Target_address_2), .Prediction(reg_file_2_1_prediction), .BUS_W(Target_address),
    .taken(Taken_or_not_taken), .RA(_3_bit_index_Read));  // open: out_10, out_11, out_12, out_13, out_14, out_15, out_16, out_17
  Register #(.width(1), .trigger("falling")) register_1 (
    .D(Prediction), .Q(Previous_Prediction), .clk(clk_t));  // open: en, clr
  and and_1 (Prediction, reg_file_2_1_prediction, write_2);

  // Other names for the same wires on the sheet: index_ID[2:0] = _3_bit_index_Write;
  //   index_IF[2:0] = _3_bit_index_Read
endmodule

module reg_file (
  input  in_1,
  input  [2:0] RA,
  input  [2:0] RW,
  input  [15:0] BUS_W,
  input  reg_write,
  input  Enable,
  output [15:0] Bus_A,
  output [15:0] out_8,
  output [15:0] out_9,
  output [15:0] out_10,
  output [15:0] out_11,
  output [15:0] out_12,
  output [15:0] out_13,
  output [15:0] out_14,
  output [15:0] out_15
);

  wire and_1_out, and_2_out, and_3_out, and_4_out, and_5_out, and_6_out, and_7_out, and_8_out,
       decoder_1_out0, decoder_1_out1, decoder_1_out2, decoder_1_out3, decoder_1_out4, decoder_1_out5,
       decoder_1_out6, decoder_1_out7;

  Decoder #(.select(3), .enable("false")) decoder_1 (
    .out0(decoder_1_out0), .out1(decoder_1_out1), .out2(decoder_1_out2), .out3(decoder_1_out3),
    .out4(decoder_1_out4), .out5(decoder_1_out5), .out6(decoder_1_out6), .out7(decoder_1_out7), .sel(RW));
  and and_1 (and_1_out, decoder_1_out0, Enable, reg_write);
  and and_2 (and_2_out, decoder_1_out1, Enable, reg_write);
  and and_3 (and_3_out, decoder_1_out2, Enable, reg_write);
  and and_4 (and_4_out, decoder_1_out3, Enable, reg_write);
  and and_5 (and_5_out, decoder_1_out4, Enable, reg_write);
  and and_6 (and_6_out, decoder_1_out5, Enable, reg_write);
  and and_7 (and_7_out, decoder_1_out6, Enable, reg_write);
  and and_8 (and_8_out, decoder_1_out7, Enable, reg_write);
  Register #(.width(16)) register_1 (.D(BUS_W), .en(and_1_out), .Q(out_8), .clk(in_1));  // open: clr
  Register #(.width(16)) register_2 (.D(BUS_W), .en(and_2_out), .Q(out_9), .clk(in_1));  // open: clr
  Register #(.width(16)) register_3 (.D(BUS_W), .en(and_3_out), .Q(out_10), .clk(in_1));  // open: clr
  Register #(.width(16)) register_4 (.D(BUS_W), .en(and_4_out), .Q(out_11), .clk(in_1));  // open: clr
  Register #(.width(16)) register_5 (.D(BUS_W), .en(and_5_out), .Q(out_12), .clk(in_1));  // open: clr
  Register #(.width(16)) register_6 (.D(BUS_W), .en(and_6_out), .Q(out_13), .clk(in_1));  // open: clr
  Register #(.width(16)) register_7 (.D(BUS_W), .en(and_7_out), .Q(out_14), .clk(in_1));  // open: clr
  Register #(.width(16)) register_8 (.D(BUS_W), .en(and_8_out), .Q(out_15), .clk(in_1));  // open: clr
  Multiplexer #(.select(3), .width(16), .disabled(0), .enable("false")) multiplexer_1 (
    .in0(out_8), .in1(out_9), .in2(out_10), .in3(out_11), .in4(out_12), .in5(out_13), .in6(out_14),
    .in7(out_15), .out(Bus_A), .sel(RA));

  // Other names for the same wires on the sheet: R0[15:0] = out_8; R1[15:0] = out_9; R2[15:0] = out_10;
  //   R3[15:0] = out_11; R4[15:0] = out_12; R5[15:0] = out_13; R6[15:0] = out_14; R7[15:0] = out_15;
  //   regwrite = reg_write
endmodule

module reg_file_2 (
  input  in_1,
  input  [2:0] RA,
  input  [2:0] RW,
  input  [15:0] BUS_W,
  input  taken,
  input  reg_write,
  input  Enable,
  output [15:0] Bus_A,
  output Prediction,
  output [15:0] out_10,
  output [15:0] out_11,
  output [15:0] out_12,
  output [15:0] out_13,
  output [15:0] out_14,
  output [15:0] out_15,
  output [15:0] out_16,
  output [15:0] out_17
);

  wire decoder_1_out0, decoder_1_out1, decoder_1_out2, decoder_1_out3, decoder_1_out4, decoder_1_out5,
       decoder_1_out6, decoder_1_out7, e0, e1, e2, e3, e4, e5, e6, e7, P0, P1, P2, P3, P4, P5, P6, P7;

  Decoder #(.select(3), .enable("false")) decoder_1 (
    .out0(decoder_1_out0), .out1(decoder_1_out1), .out2(decoder_1_out2), .out3(decoder_1_out3),
    .out4(decoder_1_out4), .out5(decoder_1_out5), .out6(decoder_1_out6), .out7(decoder_1_out7), .sel(RW));
  and and_1 (e0, decoder_1_out0, Enable, reg_write);
  and and_2 (e1, decoder_1_out1, Enable, reg_write);
  and and_3 (e2, decoder_1_out2, Enable, reg_write);
  and and_4 (e3, decoder_1_out3, Enable, reg_write);
  and and_5 (e4, decoder_1_out4, Enable, reg_write);
  and and_6 (e5, decoder_1_out5, Enable, reg_write);
  and and_7 (e6, decoder_1_out6, Enable, reg_write);
  and and_8 (e7, decoder_1_out7, Enable, reg_write);
  Register #(.width(16)) register_1 (.D(BUS_W), .en(e0), .Q(out_10), .clk(in_1));  // open: clr
  Register #(.width(16)) register_2 (.D(BUS_W), .en(e1), .Q(out_11), .clk(in_1));  // open: clr
  Register #(.width(16)) register_3 (.D(BUS_W), .en(e2), .Q(out_12), .clk(in_1));  // open: clr
  Register #(.width(16)) register_4 (.D(BUS_W), .en(e3), .Q(out_13), .clk(in_1));  // open: clr
  Register #(.width(16)) register_5 (.D(BUS_W), .en(e4), .Q(out_14), .clk(in_1));  // open: clr
  Register #(.width(16)) register_6 (.D(BUS_W), .en(e5), .Q(out_15), .clk(in_1));  // open: clr
  Register #(.width(16)) register_7 (.D(BUS_W), .en(e6), .Q(out_16), .clk(in_1));  // open: clr
  Register #(.width(16)) register_8 (.D(BUS_W), .en(e7), .Q(out_17), .clk(in_1));  // open: clr
  Brediction brediction_1 (.Taken(taken), .clk(in_1), .enable(e0), .Enable_Mux(P0));
  Brediction brediction_2 (.Taken(taken), .clk(in_1), .enable(e1), .Enable_Mux(P1));
  Brediction brediction_3 (.Taken(taken), .clk(in_1), .enable(e2), .Enable_Mux(P2));
  Brediction brediction_4 (.Taken(taken), .clk(in_1), .enable(e3), .Enable_Mux(P3));
  Brediction brediction_5 (.Taken(taken), .clk(in_1), .enable(e4), .Enable_Mux(P4));
  Brediction brediction_6 (.Taken(taken), .clk(in_1), .enable(e5), .Enable_Mux(P5));
  Brediction brediction_7 (.Taken(taken), .clk(in_1), .enable(e6), .Enable_Mux(P6));
  Brediction brediction_8 (.Taken(taken), .clk(in_1), .enable(e7), .Enable_Mux(P7));
  Multiplexer #(.select(3), .width(16), .disabled(0), .enable("false")) multiplexer_1 (
    .in0(out_10), .in1(out_11), .in2(out_12), .in3(out_13), .in4(out_14), .in5(out_15), .in6(out_16),
    .in7(out_17), .out(Bus_A), .sel(RA));
  Multiplexer #(.select(3), .disabled(0), .enable("false")) multiplexer_2 (
    .in0(P0), .in1(P1), .in2(P2), .in3(P3), .in4(P4), .in5(P5), .in6(P6), .in7(P7), .out(Prediction), .sel(RA));

  // Other names for the same wires on the sheet: R0[15:0] = out_10; R1[15:0] = out_11; R2[15:0] = out_12;
  //   R3[15:0] = out_13; R4[15:0] = out_14; R5[15:0] = out_15; R6[15:0] = out_16; R7[15:0] = out_17;
  //   regwrite = reg_write
endmodule

module Brediction (
  input  Taken,
  input  clk,
  input  enable,
  output Enable_Mux
);

  wire and_1_out, d_ff_1_q, d_ff_1_qn, d_ff_2_qn, not_1_out, or_1_out, or_2_out;
  wire [0:0] counter_1_q;

  not not_1 (not_1_out, Taken);
  D_Flip_Flop d_ff_1 (.clk(clk), .D(1'b1), .Q(d_ff_1_q), .Qn(d_ff_1_qn));  // open: preset, en, reset
  or or_1 (or_1_out, d_ff_1_qn, not_1_out);
  D_Flip_Flop d_ff_2 (.clk(clk), .D(1'b1), .Qn(d_ff_2_qn));  // open: Q, preset, en, reset
  Counter #(.width(2), .max('h3), .ongoal("stay")) counter_1 (
    .load(or_1_out), .D(2'b01), .count(d_ff_1_q), .Q({Enable_Mux, counter_1_q[0]}), .clk(and_1_out));  // open: carry, clr
  and and_1 (and_1_out, clk, or_2_out);
  or or_2 (or_2_out, d_ff_2_qn, enable);
endmodule
