// Logisim project BranchUnit1.circ as structural Verilog: 1 circuit, main circuit BranchUnit
module BranchUnit (
  input  in_1,
  input  in_2,
  input  [2:0] in_3,
  output out_4
);

  wire not_1_out, not_2_out;

  not not_1 (not_1_out, in_1);
  not not_2 (not_2_out, in_2);
  Multiplexer #(.select(3), .enable("false")) multiplexer_1 (
    .in0(1'b0), .in1(in_1), .in2(not_1_out), .in3(in_2), .in4(not_2_out), .out(out_4), .sel(in_3));  // open: in5, in6, in7
endmodule
