// Logisim project Comparator.circ as structural Verilog: 1 circuit, main circuit Comparator
module Comparator (
  input  [15:0] in_1,
  input  [15:0] in_2,
  output slt,
  output Zero
);

  wire adder_1_cout, adder_2_cout, adder_2_out, not_2_out, xor_1_out;
  wire [14:0] adder_1_out, not_1_out;

  assign not_1_out = ~in_2[14:0];  // NOT_Gate not_1, 15 bits wide
  not not_2 (not_2_out, in_2[15]);
  Adder #(.width(15)) adder_1 (.a(in_1[14:0]), .b(not_1_out), .out(adder_1_out), .cin(1'b1), .cout(adder_1_cout));
  Adder #(.width(1)) adder_2 (.a(in_1[15]), .b(not_2_out), .out(adder_2_out), .cin(adder_1_cout), .cout(adder_2_cout));
  xor xor_1 (xor_1_out, adder_1_cout, adder_2_cout);
  nor nor_1 (Zero, adder_1_out[0], adder_1_out[1], adder_1_out[2], adder_1_out[3], adder_1_out[4], adder_1_out[5], adder_1_out[6], adder_1_out[7], adder_1_out[8], adder_1_out[9], adder_1_out[10], adder_1_out[11], adder_1_out[12], adder_1_out[13], adder_1_out[14], adder_2_out);
  xor xor_2 (slt, xor_1_out, adder_2_out);

  // Notes on the sheet:
  //   <=======
  //   overflow
endmodule
