// Logisim project Hazard unit 2.circ as structural Verilog: 6 circuits, main circuit Forward A
// Forward to EX
module Hazard_unit (
  input  [2:0] Rs,
  input  [2:0] Rt,
  input  [2:0] Destination_MEM,
  input  [2:0] Destination_WB,
  input  MEM_Reg_Write,
  input  WB_Reg_Write,
  output [1:0] Forward_A_EX,
  output [1:0] Forward_B_EX
);

  Forward_A forward_a_1 (
    .Rs(Rs), .Rd2(Destination_MEM), .Rd3(Destination_WB), .MEM_RegWr(MEM_Reg_Write), .WB_RegWr(WB_Reg_Write),
    .Forward_A(Forward_A_EX));
  Forward_B forward_b_1 (
    .Rt(Rt), .Rd2(Destination_MEM), .Rd3(Destination_WB), .MEM_RegWr(MEM_Reg_Write), .WB_RegWr(WB_Reg_Write),
    .Forward_B(Forward_B_EX));

  // Other names for the same wires on the sheet: MEM_RegWr = MEM_Reg_Write; Rd2[2:0] = Destination_MEM;
  //   Rd3[2:0] = Destination_WB; WB_RegWr = WB_Reg_Write
endmodule

// Forward to ID
module Hazard_unit_2 (
  input  [2:0] Rs,
  input  [2:0] Rt,
  input  [2:0] Destination_EX,
  input  [2:0] Destination_MEM,
  input  EX_RegWr,
  input  MEM_RegWr,
  output [1:0] Forward_A_ID,
  output [1:0] Forward_B_ID
);

  Forward_A forward_a_1 (
    .Rs(Rs), .Rd2(Destination_EX), .Rd3(Destination_MEM), .MEM_RegWr(EX_RegWr), .WB_RegWr(MEM_RegWr),
    .Forward_A(Forward_A_ID));
  Forward_B forward_b_1 (
    .Rt(Rt), .Rd2(Destination_EX), .Rd3(Destination_MEM), .MEM_RegWr(EX_RegWr), .WB_RegWr(MEM_RegWr),
    .Forward_B(Forward_B_ID));

  // Other names for the same wires on the sheet: Rd2[2:0] = Destination_EX; Rd3[2:0] = Destination_MEM
endmodule

module Forward_A (
  input  [2:0] Rs,
  input  [2:0] Rd2,
  input  [2:0] Rd3,
  input  MEM_RegWr,
  input  WB_RegWr,
  output [1:0] Forward_A
);

  wire and_1_out, and_2_out, nor_1_out, nor_2_out, or_1_out, or_2_out;
  wire [2:0] subtractor_1_out, subtractor_2_out;

  Subtractor #(.width(3)) subtractor_1 (.a(Rs), .b(Rd2), .out(subtractor_1_out));  // open: bin, bout
  Subtractor #(.width(3)) subtractor_2 (.a(Rs), .b(Rd3), .out(subtractor_2_out));  // open: bin, bout
  nor nor_1 (nor_1_out, subtractor_1_out[0], subtractor_1_out[1], subtractor_1_out[2]);
  or or_1 (or_1_out, Rs[0], Rs[1], Rs[2]);
  nor nor_2 (nor_2_out, subtractor_2_out[0], subtractor_2_out[1], subtractor_2_out[2]);
  or or_2 (or_2_out, Rs[0], Rs[1], Rs[2]);
  and and_1 (and_1_out, nor_1_out, or_1_out, MEM_RegWr);
  and and_2 (and_2_out, nor_2_out, or_2_out, WB_RegWr);
  Forward_ctrl forward_ctrl_1 (.F1(and_1_out), .A1(Forward_A[1]), .A2(Forward_A[0]), .F2(and_2_out));
endmodule

module Forward_B (
  input  [2:0] Rt,
  input  [2:0] Rd2,
  input  [2:0] Rd3,
  input  MEM_RegWr,
  input  WB_RegWr,
  output [1:0] Forward_B
);

  wire and_1_out, and_2_out, nor_1_out, nor_2_out, or_1_out, or_2_out;
  wire [2:0] subtractor_1_out, subtractor_2_out;

  Subtractor #(.width(3)) subtractor_1 (.a(Rt), .b(Rd2), .out(subtractor_1_out));  // open: bin, bout
  Subtractor #(.width(3)) subtractor_2 (.a(Rt), .b(Rd3), .out(subtractor_2_out));  // open: bin, bout
  or or_1 (or_1_out, Rt[0], Rt[1], Rt[2]);
  or or_2 (or_2_out, Rt[0], Rt[1], Rt[2]);
  nor nor_1 (nor_1_out, subtractor_1_out[0], subtractor_1_out[1], subtractor_1_out[2]);
  nor nor_2 (nor_2_out, subtractor_2_out[0], subtractor_2_out[1], subtractor_2_out[2]);
  and and_1 (and_1_out, nor_1_out, or_1_out, MEM_RegWr);
  and and_2 (and_2_out, nor_2_out, or_2_out, WB_RegWr);
  Forward_ctrl forward_ctrl_1 (.F1(and_1_out), .A1(Forward_B[1]), .A2(Forward_B[0]), .F2(and_2_out));
endmodule

module Forward_ctrl (
  input  F1,
  input  F2,
  output A1,
  output A2
);

  wire not_1_out;

  not not_1 (not_1_out, F1);
  and and_1 (A1, not_1_out, F2);

  assign A2 = F1;
endmodule

module Stall (
  input  MemRead_EX,
  input  [2:0] Rt_ID_EX,
  input  [2:0] Rt_IF_ID,
  input  [2:0] Rs_IF_ID,
  output Stall
);

  wire and_1_out, and_2_out, nor_1_out, nor_2_out;
  wire [2:0] subtractor_1_out, subtractor_2_out;

  Subtractor #(.width(3)) subtractor_1 (.a(Rt_ID_EX), .b(Rt_IF_ID), .out(subtractor_1_out));  // open: bin, bout
  Subtractor #(.width(3)) subtractor_2 (.a(Rt_ID_EX), .b(Rs_IF_ID), .out(subtractor_2_out));  // open: bin, bout
  nor nor_1 (nor_1_out, subtractor_1_out[0], subtractor_1_out[1], subtractor_1_out[2]);
  nor nor_2 (nor_2_out, subtractor_2_out[0], subtractor_2_out[1], subtractor_2_out[2]);
  and and_1 (and_1_out, MemRead_EX, nor_1_out);
  and and_2 (and_2_out, MemRead_EX, nor_2_out);
  or or_1 (Stall, and_2_out, and_1_out);
endmodule
