// Logisim project Pipelined16(working).circ as structural Verilog: 6 circuits, main circuit Pipelined CPU
module Pipelined_CPU (
);

  wire alu_1_out_5, ALUSrc, ALUSrc_EX, and_1_out, and_3_out, and_4_out, branch, clk, Enable_IF_Branch_Jump,
       Flush, Is_Branch, Is_Branch_Jump_Taken, Is_J_JAL, IS_JAL, IS_JAL_EX, IS_JAL_MEM, Is_JR, IS_LUI,
       IS_LUI_EX, IS_LUI_MEM, IS_LUI_WB, Mem_Read, Mem_Read_EX, Mem_Read_ID, Mem_Read_MEM, Mem_Write,
       Mem_Write_EX, Mem_Write_ID, Mem_Write_MEM, MemToReg, MemToReg_EX, MemToReg_MEM, not_1_out, not_2_out,
       NotTaken_PC, Prediction, Previous_Prediction, Reg_Write, Reg_Write_EX, Reg_Write_ID, Reg_Write_MEM,
       Reg_Write_WB, Sign_Extend, Sign_Extend_EX, Slt, Stall, Zero;
  wire [1:0] BUS_W, BUS_W_EX, BUS_W_MEM, BUS_W_WB, Forward_B_EX, Forward_B_ID, Fowrard_A_EX, Fowrard_A_ID,
       Reg_Dst, Reg_Dst_EX;
  wire [2:0] branch_op, Destination_Reg_EX, Destination_Reg_MEM, Destination_Reg_WB, Index_Read, Index_Write,
       Rd_EX, Rs_EX, Rt_EX;
  wire [4:0] xnor_1_out, xnor_2_out;
  wire [7:0] ALUoperations, ALUoperations_EX;
  wire [10:0] _11_immediate;
  wire [15:0] _5_IMM_Extended, _5_IMM_Extended_EX, A, adder_6_out, adder_7_out, ALUOutput_EX, ALUOutput_MEM,
       B_J_Target, bit_extender_1_out, bit_extender_2_out, bit_extender_3_out, BUS_A, BUS_A_EX, BUS_B,
       BUS_B_EX, BUS_W_data_EX, BUS_W_data_MEM, I_R_Output_MEM, I_R_Output_WB, multiplexer_1_out,
       multiplexer_2_out, multiplexer_3_out, multiplexer_5_out, multiplexer_6_out, multiplexer_8_out,
       multiplexer_9_out, multiplexer_10_out, multiplexer_12_out, multiplexer_14_out, multiplexer_23_out,
       NextPC, PC_1, PC_EX, PC_ID_1, PC_MEM, PC_Target, PC_WB, PC_WB_1, R0, R1, R2, R3, R4, R5, R6, R7,
       ram_1_data, Rd1_To_EX, Rd1_To_ID, Rd2_To_EX, Rd2_To_ID, rom_1_data, Target_Branch, Target_Jump,
       upper_11_immediate_EX, upper_11_immediate_MEM, upper_11_immediate_WB;
  wire [15:3] PC, PC_ID;
  wire [15:11] Instruction_ID;

  Multiplexer #(.width(16), .enable("false")) multiplexer_1 (
    .in0(NextPC), .in1(PC_Target), .out(multiplexer_1_out), .sel(Prediction));
  Multiplexer #(.select(2), .width(16), .enable("false")) multiplexer_2 (
    .in0(BUS_A), .in1(Rd1_To_ID), .in2(Rd2_To_ID), .out(multiplexer_2_out), .sel(Fowrard_A_ID));  // open: in3
  assign bit_extender_1_out = {{5{_11_immediate[10]}}, _11_immediate};  // Bit_Extender bit_extender_1
  Multiplexer #(.width(16), .enable("false")) multiplexer_3 (
    .in0(multiplexer_1_out), .in1(multiplexer_2_out), .out(multiplexer_3_out), .sel(and_1_out));
  and and_1 (and_1_out, Flush, Is_JR);
  BTB btb_1 (
    .Recent_branch_adddress({PC_ID, Index_Write}), .Target_address(B_J_Target), .CLK(clk),
    .Target_address_2(PC_Target), .Taken_or_not_taken(Is_Branch_Jump_Taken),
    .Previous_Prediction(Previous_Prediction), .Prediction(Prediction), .Current_PC({PC, Index_Read}),
    ._3_bit_index_Write(Index_Write), ._3_bit_index_Read(Index_Read),
    .Enable_if_branch_jump(Enable_IF_Branch_Jump));
  Adder #(.width(16)) adder_1 (.a({PC_ID, Index_Write}), .b(_5_IMM_Extended), .out(Target_Branch));  // open: cin, cout
  Register #(.width(16)) register_1 (
    .D(multiplexer_3_out), .en(not_1_out), .Q({PC, Index_Read}), .clk(clk));  // open: clr
  not not_1 (not_1_out, Stall);
  // Probe on B_J_Target
  Multiplexer #(.width(16), .enable("false")) multiplexer_4 (
    .in0(Target_Branch), .in1(Target_Jump), .out(B_J_Target), .sel(Is_J_JAL));
  Adder #(.width(16)) adder_2 (.a(16'h1), .b(PC_WB), .out(PC_WB_1));  // open: cin, cout
  or or_1 (Is_Branch, branch_op[0], branch_op[1], branch_op[2]);
  and and_2 (NotTaken_PC, Flush, ~Is_Branch_Jump_Taken);  // AND_Gate
  or or_2 (Is_Branch_Jump_Taken, branch, Is_J_JAL, Is_JR);
  or or_3 (Enable_IF_Branch_Jump, Is_JR, Is_J_JAL, Is_Branch);
  Adder #(.width(16)) adder_3 (.a({PC_ID, Index_Write}), .b(bit_extender_1_out), .out(Target_Jump));  // open: cin, cout
  Multiplexer #(.width(16), .enable("false")) multiplexer_5 (
    .in0(PC_1), .in1(PC_ID_1), .out(multiplexer_5_out), .sel(NotTaken_PC));
  Adder #(.width(16)) adder_4 (.a({PC_ID, Index_Write}), .b(16'h1), .out(PC_ID_1));  // open: cin, cout
  Adder #(.width(16)) adder_5 (.a(16'h1), .b({PC, Index_Read}), .out(PC_1));  // open: cin, cout
  Multiplexer #(.width(16), .enable("false")) multiplexer_6 (
    .in0(multiplexer_5_out), .in1(Target_Branch), .out(multiplexer_6_out), .sel(and_3_out));
  and and_3 (and_3_out, Flush, branch);
  ROM #(.addrWidth(16), .dataWidth(16)) rom_1 (.addr({PC, Index_Read}), .data(rom_1_data));  // open: sel
  and and_4 (and_4_out, Flush, Is_J_JAL);
  Multiplexer #(.width(16), .enable("false")) multiplexer_7 (
    .in0(multiplexer_6_out), .in1(Target_Jump), .out(NextPC), .sel(and_4_out));
  IF_ID IF_ID (
    .CLK(clk), .PC_IF({PC, Index_Read}), .Instruction_IF(rom_1_data), .PC_ID({PC_ID, Index_Write}),
    .Instruction_ID({Instruction_ID, _11_immediate}), .Stall(Stall), .Flush(Flush));
  // Probe on {Instruction_ID, _11_immediate}
  Control_Unit control_unit_1 (
    .Opcode(Instruction_ID), .Function(_11_immediate[10:9]), .ALUSrc(ALUSrc), .Sign_Extend(Sign_Extend),
    .Mem_write(Mem_Write), .Mem_read(Mem_Read), .Mem_to_Reg(MemToReg), .BUS_W(BUS_W), .RegDst(Reg_Dst),
    .Reg_write(Reg_Write), .is_J_JAL(Is_J_JAL), .Branch_op(branch_op), .is_JR(Is_JR),
    .ALU_Operations(ALUoperations));
  Multiplexer #(.select(2), .width(16), .enable("false")) multiplexer_8 (
    .in0(BUS_A), .in1(Rd1_To_ID), .in2(Rd2_To_ID), .out(multiplexer_8_out), .sel(Fowrard_A_ID));  // open: in3
  Multiplexer #(.select(2), .width(16), .enable("false")) multiplexer_9 (
    .in0(BUS_B), .in1(Rd1_To_ID), .in2(Rd2_To_ID), .out(multiplexer_9_out), .sel(Forward_B_ID));  // open: in3
  Adder #(.width(16)) adder_6 (.a(PC_EX), .b(16'h1), .out(adder_6_out));  // open: cin, cout
  Adder #(.width(16)) adder_7 (.a(PC_MEM), .b(16'h1), .out(adder_7_out));  // open: cin, cout
  Comparator comparator_1 (.in_1(multiplexer_8_out), .slt(Slt), .in_2(multiplexer_9_out), .Zero(Zero));
  BranchUnit branchunit_1 (.in_1(Zero), .in_2(Slt), .in_3(branch_op), .out_4(branch));
  // Probe on {PC, Index_Read}
  // Probe on R0
  // Probe on R1
  // Probe on R2
  // Probe on R3
  // Probe on R4
  // Probe on R5
  // Probe on R6
  // Probe on R7
  // OR_Gate or_4 has open pins: in0=Stall, in1=Flush, out=open
  Multiplexer #(.width(16), .enable("false")) multiplexer_10 (
    .in0(ALUOutput_EX), .in1(upper_11_immediate_EX), .out(multiplexer_10_out), .sel(IS_LUI_EX));
  Multiplexer #(.width(16), .enable("false")) multiplexer_11 (
    .in0(multiplexer_10_out), .in1(adder_6_out), .out(Rd1_To_ID), .sel(IS_JAL_EX));
  Multiplexer #(.width(16), .enable("false")) multiplexer_12 (
    .in0(I_R_Output_MEM), .in1(upper_11_immediate_MEM), .out(multiplexer_12_out), .sel(IS_LUI_MEM));
  Multiplexer #(.width(16), .enable("false")) multiplexer_13 (
    .in0(multiplexer_12_out), .in1(adder_7_out), .out(Rd2_To_ID), .sel(IS_JAL_MEM));
  Hazard_unit_2 hazard_unit_2_1 (
    .Rs(_11_immediate[5:3]), .Rt(_11_immediate[2:0]), .Destination_EX(Destination_Reg_EX),
    .Destination_MEM(Destination_Reg_MEM), .EX_RegWr(Reg_Write_EX), .MEM_RegWr(Reg_Write_MEM),
    .Forward_A_ID(Fowrard_A_ID), .Forward_B_ID(Forward_B_ID));
  Counter #(.width(32), .max('hffffffff)) counter_1 (.count(Flush), .clk(clk));  // open: load, D, Q, carry, clr
  register_file_main main_1 (
    .RW(Destination_Reg_WB), .BUS_W(multiplexer_14_out), .RA(_11_immediate[5:3]), .Bus_A(BUS_A),
    .Bus_B(BUS_B), .RB(_11_immediate[2:0]), .reg_write(Reg_Write_WB), .out_9(R0), .out_10(R1), .out_11(R2),
    .out_12(R3), .out_13(R4), .out_14(R5), .out_15(R6), .out_16(R7), .in_1(not_2_out));
  assign bit_extender_2_out = {{11{1'b0}}, _11_immediate[10:6]};  // Bit_Extender bit_extender_2
  assign bit_extender_3_out = {{11{_11_immediate[10]}}, _11_immediate[10:6]};  // Bit_Extender bit_extender_3
  Counter #(.width(32), .max('hf4240), .ongoal("stay")) counter_2 (.clk(clk));  // open: load, D, count, Q, carry, clr
  Clock clock_1 (.out(clk));
  not not_2 (not_2_out, clk);
  Multiplexer #(.select(2), .width(16), .enable("false")) multiplexer_14 (
    .in0(I_R_Output_WB), .in2(upper_11_immediate_WB), .in3(PC_WB_1), .out(multiplexer_14_out), .sel(BUS_W_WB));  // open: in1
  Multiplexer #(.width(16), .enable("false")) multiplexer_15 (
    .in0(bit_extender_2_out), .in1(bit_extender_3_out), .out(_5_IMM_Extended), .sel(Sign_Extend));
  Multiplexer #(.enable("false")) multiplexer_16 (.in0(Mem_Read), .in1(1'b0), .out(Mem_Read_ID), .sel(Stall));
  Multiplexer #(.enable("false")) multiplexer_17 (.in0(Reg_Write), .in1(1'b0), .out(Reg_Write_ID), .sel(Stall));
  Multiplexer #(.enable("false")) multiplexer_18 (.in0(Mem_Write), .in1(1'b0), .out(Mem_Write_ID), .sel(Stall));
  ID_EX id_ex_1 (
    .BUSW_ID(BUS_W), .ALUOperation_ID(ALUoperations), .BUSA_ID(BUS_A), .CLK(clk), .RegDst_ID(Reg_Dst),
    .BUSB_ID(BUS_B), .REGWrite_ID(Reg_Write_ID), .MEMREAD_ID(Mem_Read_ID), .ALUSrc_ID(ALUSrc),
    .Rt_ID(_11_immediate[2:0]), .MEMWRITE_ID(Mem_Write_ID), .SignExtend_ID(Sign_Extend),
    .Rd_ID(_11_immediate[8:6]), .BUSW_EX(BUS_W_EX), .ALUOperation_EX(ALUoperations_EX), .BUSA_EX(BUS_A_EX),
    .RegDst_EX(Reg_Dst_EX), .BUSB_EX(BUS_B_EX), .REGWrite_EX(Reg_Write_EX), .MEMREAD_EX(Mem_Read_EX),
    .ALUSrc_EX(ALUSrc_EX), .Rt_EX(Rt_EX), .MEMWRITE_EX(Mem_Write_EX), .SignExtend_EX(Sign_Extend_EX),
    .Rd_EX(Rd_EX), .PC_ID({PC_ID, Index_Write}), .PC_EX(PC_EX), .Rs_ID(_11_immediate[5:3]), .Rs_EX(Rs_EX),
    .Upper11IMM_ID({_11_immediate, {5{1'b0}}}), .Upper11IMM_EX(upper_11_immediate_EX),
    ._5_IMM_Extended(_5_IMM_Extended), ._5_IMM_Extended_EX(_5_IMM_Extended_EX), .MEM_TO_REG_ID(MemToReg),
    .MEM_TO_REG_EX(MemToReg_EX), .IS_LUI_ID(IS_LUI), .IS_LUI_EX(IS_LUI_EX), .IS_JAL_ID(IS_JAL),
    .IS_JAL_EX(IS_JAL_EX));
  Stall stall_1 (
    .MemRead_EX(Mem_Read_EX), .Rt_ID_EX(Rt_EX), .Rt_IF_ID(_11_immediate[2:0]), .Rs_IF_ID(_11_immediate[5:3]),
    .Stall(Stall));
  assign xnor_1_out = ~(Instruction_ID ^ 5'b10010);  // XNOR_Gate xnor_1, 5 bits wide
  assign xnor_2_out = ~(Instruction_ID ^ {5{1'b1}});  // XNOR_Gate xnor_2, 5 bits wide
  and and_5 (IS_LUI, xnor_1_out[0], xnor_1_out[1], xnor_1_out[2], xnor_1_out[3], xnor_1_out[4]);
  and and_6 (IS_JAL, xnor_2_out[0], xnor_2_out[1], xnor_2_out[2], xnor_2_out[3], xnor_2_out[4]);
  Multiplexer #(.select(2), .width(16), .enable("false")) multiplexer_19 (
    .in0(BUS_A_EX), .in1(Rd1_To_EX), .in2(Rd2_To_EX), .out(A), .sel(Fowrard_A_EX));  // open: in3
  Multiplexer #(.select(2), .width(16), .enable("false")) multiplexer_20 (
    .in0(BUS_B_EX), .in1(Rd1_To_EX), .in2(Rd2_To_EX), .out(BUS_W_data_EX), .sel(Forward_B_EX));  // open: in3
  Multiplexer #(.select(2), .width(3), .enable("false")) multiplexer_21 (
    .in0(Rt_EX), .in1(Rd_EX), .in2(3'b001), .in3(3'b111), .out(Destination_Reg_EX), .sel(Reg_Dst_EX));
  Multiplexer #(.width(16), .enable("false")) multiplexer_22 (
    .in0(ALUOutput_MEM), .in1(upper_11_immediate_MEM), .out(Rd1_To_EX), .sel(IS_LUI_MEM));
  xor xor_1 (Flush, Is_Branch_Jump_Taken, Previous_Prediction);
  Hazard_unit hazard_unit_1 (
    .Rs(Rs_EX), .Rt(Rt_EX), .Destination_MEM(Destination_Reg_MEM), .Destination_WB(Destination_Reg_WB),
    .MEM_Reg_Write(Reg_Write_MEM), .WB_Reg_Write(Reg_Write_WB), .Forward_A_EX(Fowrard_A_EX),
    .Forward_B_EX(Forward_B_EX));
  Multiplexer #(.width(16), .enable("false")) multiplexer_23 (
    .in0(BUS_W_data_EX), .in1(_5_IMM_Extended_EX), .out(multiplexer_23_out), .sel(ALUSrc_EX));
  Multiplexer #(.width(16), .enable("false")) multiplexer_24 (
    .in0(I_R_Output_WB), .in1(upper_11_immediate_WB), .out(Rd2_To_EX), .sel(IS_LUI_WB));
  ALU alu_1 (
    .in_1(A), .in_2(multiplexer_23_out), .in_3(ALUoperations_EX), .out_6(ALUOutput_EX), .out_5(alu_1_out_5));  // open: out_4
  EX_MEM EX_MEM (
    .ALUOutput_EX(ALUOutput_EX), .BUSW_EX(BUS_W_EX), .MEMREAD_EX(Mem_Read_EX), .BUSW_EX_2(BUS_W_data_EX),
    .MEMWRITE_EX(Mem_Write_EX), .REGWrite_EX(Reg_Write_EX), .Destination_Reg_EX(Destination_Reg_EX),
    .ALUOutput_MEM(ALUOutput_MEM), .BUSW_MEM(BUS_W_MEM), .MEMREAD_MEM(Mem_Read_MEM),
    .BUSW_MEM_2(BUS_W_data_MEM), .MEMWRITE_MEM(Mem_Write_MEM), .REGWrite_MEM(Reg_Write_MEM),
    .Destination_Reg_MEM(Destination_Reg_MEM), .CLK(clk), .PC_EX(PC_EX), .PC_MEM(PC_MEM),
    .Upper11IMM_EX(upper_11_immediate_EX), .Upper11IMM_MEM(upper_11_immediate_MEM), .IS_LUI_EX(IS_LUI_EX),
    .IS_LUI_MEM(IS_LUI_MEM), .MEM_TO_REG_EX(MemToReg_EX), .MEM_TO_REG_MEM(MemToReg_MEM),
    .IS_JAL_EX(IS_JAL_EX), .IS_JAL_MEM(IS_JAL_MEM));
  RAM #(.addrWidth(16), .dataWidth(16), .bus("separate")) ram_1 (
    .addr(ALUOutput_MEM), .din(BUS_W_data_MEM), .data(ram_1_data), .str(Mem_Write_MEM), .clk(clk),
    .ld(Mem_Read_MEM));  // open: sel, clr
  Multiplexer #(.width(16), .enable("false")) multiplexer_25 (
    .in0(ALUOutput_MEM), .in1(ram_1_data), .out(I_R_Output_MEM), .sel(MemToReg_MEM));
  MEM_WB MEM_WB (
    .I_ROutput_MEM(I_R_Output_MEM), .BUSW_MEM(BUS_W_MEM), .REGWrite_MEM(Reg_Write_MEM),
    .Destination_Reg_MEM(Destination_Reg_MEM), .I_ROutput_WB(I_R_Output_WB), .BUSW_WB(BUS_W_WB),
    .REGWrite_WB(Reg_Write_WB), .Destination_Reg_WB(Destination_Reg_WB), .CLK(clk), .PC_MEM(PC_MEM),
    .PC_WB(PC_WB), .Upper11IMM_MEM(upper_11_immediate_MEM), .Upper11IMM_WB(upper_11_immediate_WB),
    .IS_LUI_MEM(IS_LUI_MEM), .IS_LUI_WB(IS_LUI_WB));

  // Other names for the same wires on the sheet: OP[4:0] = Instruction_ID; PC[2:0] = Index_Read;
  //   PC_ID[2:0] = Index_Write; Rd1_EX_To_ID[15:0] = ALUOutput_EX; Rd1_MEM_To_EX[15:0] = ALUOutput_MEM;
  //   Rd2_MEM_To_ID[15:0] = I_R_Output_MEM; Rd2_WB_To_EX[15:0] = I_R_Output_WB; Instruction_ID[10:0] = _11_immediate;
  //   Rt[2:0] = _11_immediate[2:0]; upper_11_immediate[15:5] = _11_immediate; Rs[2:0] = _11_immediate[5:3];
  //   Rd[2:0] = _11_immediate[8:6]; F[1:0] = _11_immediate[10:9]

  // Notes on the sheet:
  //   contents of rom_1 (hex, n*v repeats v):
  //   9000 2849 6801 9000 284a 840 6842 9000 2a8b 840 6883 9001 2f0b 840 9218 2a89 6819 939a 288a 840 685a
  //   880 8c0 9384 3b4d 4cd 6001 6042 6083 3aa4 b24 914 d93 70f0 88a 7700 6804 f804 4193 58de 7000 353
  //   6001 614a 618b 113 6804 1038
  //   Wasted Cycles Counter
  //   Rs
  //   Rt
  //   Rd
  //   5_immediate
  //   Total Cycles Counter
endmodule

module IF_ID (
  input  CLK,
  input  [15:0] PC_IF,
  input  [15:0] Instruction_IF,
  input  Stall,
  input  Flush,
  output [15:0] PC_ID,
  output [15:0] Instruction_ID
);

  wire not_1_out, undriven;
  wire [15:0] multiplexer_1_out;

  Register #(.width(16)) PC (.D(PC_IF), .en(not_1_out), .Q(PC_ID), .clk(CLK), .clr(undriven));
  Register #(.width(16)) Instruction (
    .D(multiplexer_1_out), .en(not_1_out), .Q(Instruction_ID), .clk(CLK));  // open: clr
  Multiplexer #(.width(16)) multiplexer_1 (
    .in0(Instruction_IF), .in1({16{1'b0}}), .out(multiplexer_1_out), .sel(Flush), .en(not_1_out));
  not not_1 (not_1_out, Stall);
endmodule

module ID_EX (
  input  [1:0] BUSW_ID,
  input  MEMREAD_ID,
  input  [7:0] ALUOperation_ID,
  input  [15:0] BUSA_ID,
  input  CLK,
  input  [1:0] RegDst_ID,
  input  [15:0] BUSB_ID,
  input  REGWrite_ID,
  input  MEMWRITE_ID,
  input  ALUSrc_ID,
  input  [2:0] Rt_ID,
  input  IS_LUI_ID,
  input  MEM_TO_REG_ID,
  input  [2:0] Rd_ID,
  input  SignExtend_ID,
  input  [2:0] Rs_ID,
  input  [15:0] Upper11IMM_ID,
  input  [15:0] PC_ID,
  input  [15:0] _5_IMM_Extended,
  input  IS_JAL_ID,
  output [1:0] BUSW_EX,
  output MEMREAD_EX,
  output [7:0] ALUOperation_EX,
  output [15:0] BUSA_EX,
  output [1:0] RegDst_EX,
  output [15:0] BUSB_EX,
  output REGWrite_EX,
  output MEMWRITE_EX,
  output ALUSrc_EX,
  output [2:0] Rt_EX,
  output IS_LUI_EX,
  output MEM_TO_REG_EX,
  output [2:0] Rd_EX,
  output SignExtend_EX,
  output [2:0] Rs_EX,
  output [15:0] Upper11IMM_EX,
  output [15:0] PC_EX,
  output [15:0] _5_IMM_Extended_EX,
  output IS_JAL_EX
);

  Register #(.width(16)) register_1 (.D(BUSA_ID), .Q(BUSA_EX), .clk(CLK));  // open: en, clr
  Register #(.width(16)) register_2 (.D(BUSB_ID), .Q(BUSB_EX), .clk(CLK));  // open: en, clr
  Register #(.width(3)) register_3 (.D(Rt_ID), .Q(Rt_EX), .clk(CLK));  // open: en, clr
  Register #(.width(3)) register_4 (.D(Rd_ID), .Q(Rd_EX), .clk(CLK));  // open: en, clr
  Register #(.width(3)) register_5 (.D(Rs_ID), .Q(Rs_EX), .clk(CLK));  // open: en, clr
  Register #(.width(16)) register_6 (.D(Upper11IMM_ID), .Q(Upper11IMM_EX), .clk(CLK));  // open: en, clr
  Register #(.width(16)) register_7 (.D(PC_ID), .Q(PC_EX), .clk(CLK));  // open: en, clr
  Register #(.width(16)) register_8 (.D(_5_IMM_Extended), .Q(_5_IMM_Extended_EX), .clk(CLK));  // open: en, clr
  Register #(.width(1)) register_9 (.D(IS_JAL_ID), .Q(IS_JAL_EX), .clk(CLK));  // open: en, clr
  Register #(.width(2)) register_10 (.D(BUSW_ID), .Q(BUSW_EX), .clk(CLK));  // open: en, clr
  Register #(.width(1)) register_11 (.D(REGWrite_ID), .Q(REGWrite_EX), .clk(CLK));  // open: en, clr
  Register #(.width(1)) register_12 (.D(IS_LUI_ID), .Q(IS_LUI_EX), .clk(CLK));  // open: en, clr
  Register #(.width(1)) register_13 (.D(MEMREAD_ID), .Q(MEMREAD_EX), .clk(CLK));  // open: en, clr
  Register #(.width(1)) register_14 (.D(MEMWRITE_ID), .Q(MEMWRITE_EX), .clk(CLK));  // open: en, clr
  Register #(.width(1)) register_15 (.D(MEM_TO_REG_ID), .Q(MEM_TO_REG_EX), .clk(CLK));  // open: en, clr
  Register register_16 (.D(ALUOperation_ID), .Q(ALUOperation_EX), .clk(CLK));  // open: en, clr
  Register #(.width(2)) register_17 (.D(RegDst_ID), .Q(RegDst_EX), .clk(CLK));  // open: en, clr
  Register #(.width(1)) register_18 (.D(ALUSrc_ID), .Q(ALUSrc_EX), .clk(CLK));  // open: en, clr
  Register #(.width(1)) register_19 (.D(SignExtend_ID), .Q(SignExtend_EX), .clk(CLK));  // open: en, clr

  // Notes on the sheet:
  //   WB
  //   MEM
  //   EX
endmodule

module EX_MEM (
  input  CLK,
  input  [15:0] ALUOutput_EX,
  input  [1:0] BUSW_EX,
  input  MEMREAD_EX,
  input  IS_LUI_EX,
  input  [15:0] BUSW_EX_2,
  input  MEMWRITE_EX,
  input  REGWrite_EX,
  input  MEM_TO_REG_EX,
  input  [2:0] Destination_Reg_EX,
  input  [15:0] Upper11IMM_EX,
  input  [15:0] PC_EX,
  input  IS_JAL_EX,
  output [15:0] ALUOutput_MEM,
  output [1:0] BUSW_MEM,
  output MEMREAD_MEM,
  output IS_LUI_MEM,
  output [15:0] BUSW_MEM_2,
  output MEMWRITE_MEM,
  output REGWrite_MEM,
  output MEM_TO_REG_MEM,
  output [2:0] Destination_Reg_MEM,
  output [15:0] Upper11IMM_MEM,
  output [15:0] PC_MEM,
  output IS_JAL_MEM
);

  Register #(.width(16)) register_1 (.D(ALUOutput_EX), .Q(ALUOutput_MEM), .clk(CLK));  // open: en, clr
  Register #(.width(16)) register_2 (.D(BUSW_EX_2), .Q(BUSW_MEM_2), .clk(CLK));  // open: en, clr
  Register #(.width(3)) register_3 (.D(Destination_Reg_EX), .Q(Destination_Reg_MEM), .clk(CLK));  // open: en, clr
  Register #(.width(16)) register_4 (.D(Upper11IMM_EX), .Q(Upper11IMM_MEM), .clk(CLK));  // open: en, clr
  Register #(.width(16)) register_5 (.D(PC_EX), .Q(PC_MEM), .clk(CLK));  // open: en, clr
  Register #(.width(1)) register_6 (.D(IS_JAL_EX), .Q(IS_JAL_MEM), .clk(CLK));  // open: en, clr
  Register #(.width(2)) register_7 (.D(BUSW_EX), .Q(BUSW_MEM), .clk(CLK));  // open: en, clr
  Register #(.width(1)) register_8 (.D(IS_LUI_EX), .Q(IS_LUI_MEM), .clk(CLK));  // open: en, clr
  Register #(.width(1)) register_9 (.D(REGWrite_EX), .Q(REGWrite_MEM), .clk(CLK));  // open: en, clr
  Register #(.width(1)) register_10 (.D(MEMREAD_EX), .Q(MEMREAD_MEM), .clk(CLK));  // open: en, clr
  Register #(.width(1)) register_11 (.D(MEMWRITE_EX), .Q(MEMWRITE_MEM), .clk(CLK));  // open: en, clr
  Register #(.width(1)) register_12 (.D(MEM_TO_REG_EX), .Q(MEM_TO_REG_MEM), .clk(CLK));  // open: en, clr

  // Notes on the sheet:
  //   WB
  //   MEM
endmodule

module MEM_WB (
  input  CLK,
  input  [15:0] I_ROutput_MEM,
  input  [1:0] BUSW_MEM,
  input  REGWrite_MEM,
  input  [2:0] Destination_Reg_MEM,
  input  [15:0] Upper11IMM_MEM,
  input  IS_LUI_MEM,
  input  [15:0] PC_MEM,
  output [15:0] I_ROutput_WB,
  output [1:0] BUSW_WB,
  output REGWrite_WB,
  output [2:0] Destination_Reg_WB,
  output [15:0] Upper11IMM_WB,
  output IS_LUI_WB,
  output [15:0] PC_WB
);

  Register #(.width(16)) register_1 (.D(I_ROutput_MEM), .Q(I_ROutput_WB), .clk(CLK));  // open: en, clr
  Register #(.width(3)) register_2 (.D(Destination_Reg_MEM), .Q(Destination_Reg_WB), .clk(CLK));  // open: en, clr
  Register #(.width(16)) register_3 (.D(Upper11IMM_MEM), .Q(Upper11IMM_WB), .clk(CLK));  // open: en, clr
  Register #(.width(16)) register_4 (.D(PC_MEM), .Q(PC_WB), .clk(CLK));  // open: en, clr
  Register #(.width(2)) register_5 (.D(BUSW_MEM), .Q(BUSW_WB), .clk(CLK));  // open: en, clr
  Register #(.width(1)) register_6 (.D(REGWrite_MEM), .Q(REGWrite_WB), .clk(CLK));  // open: en, clr
  Register #(.width(1)) register_7 (.D(IS_LUI_MEM), .Q(IS_LUI_WB), .clk(CLK));  // open: en, clr

  // Notes on the sheet:
  //   WB
endmodule

module Flush_ctrl (
  input  branch,
  input  enable_btb,
  input  Enable_PC,
  output out
);

  wire and_1_out, and_2_out, not_1_out, not_2_out;

  not not_1 (not_1_out, branch);
  not not_2 (not_2_out, Enable_PC);
  and and_1 (and_1_out, not_1_out, enable_btb, Enable_PC);
  and and_2 (and_2_out, branch, enable_btb, not_2_out);
  or or_1 (out, and_1_out, and_2_out);
endmodule
