// Logisim project ctrlunit1.circ as structural Verilog: 6 circuits, main circuit Control Unit
module Control_Unit (
  input  [4:0] Opcode,
  input  [1:0] Function,
  output ALUSrc,
  output Sign_Extend,
  output Mem_write,
  output Mem_read,
  output Mem_to_Reg,
  output [1:0] BUS_W,
  output [1:0] RegDst,
  output Reg_write,
  output is_J_JAL,
  output [2:0] Branch_op,
  output is_JR,
  output [7:0] ALU_Operations
);

  // Probe on Opcode
  Main_Ctrl_unit main_ctrl_unit_1 (
    .B4(Opcode[4]), .B3(Opcode[3]), .B2(Opcode[2]), .B1(Opcode[1]), .B0(Opcode[0]), .ALUSrc(ALUSrc),
    .sign_ex(Sign_Extend), .Mem_write(Mem_write), .Mem_read(Mem_read), .MemToReg(Mem_to_Reg),
    .BUS_W_1(BUS_W[1]), .BUS_W_2(BUS_W[0]), .Reg_Dst_1(RegDst[1]), .Reg_Dst_2(RegDst[0]),
    .Reg_write(Reg_write));
  PC_Ctrl_Unit pc_ctrl_unit_1 (
    .B4(Opcode[4]), .J_JAL(is_J_JAL), .B3(Opcode[3]), .Branch_op_1(Branch_op[2]), .B2(Opcode[2]),
    .B1(Opcode[1]), .B0(Opcode[0]), .Branch_op_2(Branch_op[1]), .Branch_op_3(Branch_op[0]), .is_JR(is_JR));
  ALU_Ctrl_Unit alu_ctrl_unit_1 (.Opcode(Opcode), .Function(Function), .ALU_Operations(ALU_Operations));
endmodule

// Main Ctrl Unit
module Main_Ctrl_unit (
  input  B4,
  input  B3,
  input  B2,
  input  B1,
  input  B0,
  output ALUSrc,
  output sign_ex,
  output Mem_write,
  output Mem_read,
  output MemToReg,
  output BUS_W_1,
  output BUS_W_2,
  output Reg_Dst_1,
  output Reg_Dst_2,
  output Reg_write
);

  wire and_3_out, and_4_out, and_5_out, and_6_out, and_7_out, and_8_out, and_11_out, and_12_out, and_13_out,
       and_14_out, and_15_out, and_16_out, and_17_out, and_18_out, not_1_out, not_2_out, not_3_out,
       not_4_out, not_5_out, not_6_out, not_7_out, not_8_out, not_9_out, not_10_out, not_11_out, not_12_out,
       not_13_out, not_14_out, not_15_out, not_16_out, not_17_out, not_18_out, not_19_out, not_20_out,
       not_21_out;

  not not_1 (not_1_out, B3);
  not not_2 (not_2_out, B2);
  not not_3 (not_3_out, B1);
  not not_4 (not_4_out, B3);
  not not_5 (not_5_out, B4);
  not not_6 (not_6_out, B1);
  not not_7 (not_7_out, B4);
  not not_8 (not_8_out, B1);
  not not_9 (not_9_out, B0);
  and and_1 (MemToReg, B3, B2);
  and and_2 (BUS_W_2, B4, B3);
  not not_10 (not_10_out, B3);
  not not_11 (not_11_out, B2);
  not not_12 (not_12_out, B1);
  not not_13 (not_13_out, B4);
  not not_14 (not_14_out, B3);
  not not_15 (not_15_out, B1);
  not not_16 (not_16_out, B4);
  not not_17 (not_17_out, B1);
  not not_18 (not_18_out, B0);
  not not_19 (not_19_out, B3);
  not not_20 (not_20_out, B2);
  not not_21 (not_21_out, B3);
  and and_3 (and_3_out, not_1_out, B2);
  and and_4 (and_4_out, B3, not_2_out);
  and and_5 (and_5_out, B3, not_3_out);
  and and_6 (and_6_out, B4, B1);
  and and_7 (and_7_out, not_4_out, B1, B0);
  and and_8 (and_8_out, B3, B2);
  and and_9 (Mem_write, not_5_out, B3, B2, not_6_out, B0);
  and and_10 (Mem_read, not_7_out, B3, B2, not_8_out, not_9_out);
  and and_11 (and_11_out, not_10_out, not_11_out, not_12_out);
  and and_12 (and_12_out, B4, B3);
  and and_13 (and_13_out, not_13_out, not_14_out, not_15_out);
  and and_14 (and_14_out, not_16_out, not_17_out, not_18_out);
  and and_15 (and_15_out, not_19_out, B2);
  and and_16 (and_16_out, B3, not_20_out);
  and and_17 (and_17_out, B4, not_21_out, B1);
  and and_18 (and_18_out, B4, B3, B0);
  or or_1 (ALUSrc, and_3_out, and_4_out, and_5_out, and_6_out);
  or or_2 (sign_ex, and_7_out, and_8_out, B4);
  or or_3 (Reg_Dst_2, and_11_out, and_12_out);
  or or_4 (Reg_write, and_13_out, and_14_out, and_15_out, and_16_out, and_17_out, and_18_out);

  assign BUS_W_1 = B4;
  assign Reg_Dst_1 = B4;
endmodule

module PC_Ctrl_Unit (
  input  B4,
  input  B3,
  input  B2,
  input  B1,
  input  B0,
  output J_JAL,
  output Branch_op_1,
  output Branch_op_2,
  output Branch_op_3,
  output is_JR
);

  wire and_3_out, and_4_out, and_5_out, and_6_out, and_7_out, not_1_out, not_2_out, not_3_out, not_4_out,
       not_5_out, not_6_out, not_7_out, not_8_out, not_9_out, not_10_out, not_11_out, not_12_out, not_13_out,
       not_14_out, not_15_out, not_16_out, not_17_out;

  and and_1 (J_JAL, B4, B3, B2, B1);
  not not_1 (not_1_out, B3);
  not not_2 (not_2_out, B2);
  not not_3 (not_3_out, B1);
  not not_4 (not_4_out, B4);
  not not_5 (not_5_out, B3);
  not not_6 (not_6_out, B2);
  not not_7 (not_7_out, B1);
  not not_8 (not_8_out, B0);
  not not_9 (not_9_out, B4);
  not not_10 (not_10_out, B0);
  not not_11 (not_11_out, B3);
  not not_12 (not_12_out, B2);
  not not_13 (not_13_out, B1);
  not not_14 (not_14_out, B0);
  not not_15 (not_15_out, B4);
  not not_16 (not_16_out, B3);
  not not_17 (not_17_out, B2);
  and and_2 (Branch_op_1, B4, not_1_out, not_2_out, not_3_out, B0);
  and and_3 (and_3_out, not_4_out, B3, B2, B1, B0);
  and and_4 (and_4_out, B4, not_5_out, not_6_out, not_7_out, not_8_out);
  and and_5 (and_5_out, not_9_out, B3, B2, B1, not_10_out);
  and and_6 (and_6_out, B4, not_11_out, not_12_out, not_13_out, not_14_out);
  and and_7 (and_7_out, B4, B3, B2, B1, B0);
  and and_8 (is_JR, not_15_out, not_16_out, not_17_out, B1);
  or or_1 (Branch_op_2, and_3_out, and_4_out);
  or or_2 (Branch_op_3, and_5_out, and_6_out, and_7_out);
endmodule

module R_type_ALU_Ctrl (
  input  B0,
  input  B1,
  input  B2,
  input  B3,
  input  B4,
  input  B5,
  input  B6,
  output a1,
  output a2,
  output a3,
  output a4,
  output a5,
  output a6,
  output a7,
  output a8
);

  wire and_2_out, and_3_out, and_4_out, and_6_out, and_7_out, and_8_out, and_9_out, and_10_out, not_1_out,
       not_2_out, not_3_out, not_4_out, not_5_out, not_6_out, not_7_out, not_8_out, not_9_out, not_10_out,
       not_11_out, not_12_out, not_13_out, not_14_out, not_15_out, not_16_out, not_17_out, not_18_out,
       not_19_out, not_20_out, not_21_out, not_22_out, not_23_out, not_24_out, not_25_out, not_26_out,
       not_27_out, not_28_out, not_29_out, not_30_out, not_31_out, not_32_out, not_33_out, not_34_out,
       not_35_out, not_36_out, not_37_out, not_38_out, not_39_out, not_40_out, not_41_out, not_42_out,
       not_43_out, not_44_out, not_45_out, not_46_out;

  not not_1 (not_1_out, B0);
  not not_2 (not_2_out, B1);
  not not_3 (not_3_out, B2);
  not not_4 (not_4_out, B3);
  not not_5 (not_5_out, B4);
  not not_6 (not_6_out, B0);
  not not_7 (not_7_out, B1);
  not not_8 (not_8_out, B2);
  not not_9 (not_9_out, B3);
  not not_10 (not_10_out, B0);
  not not_11 (not_11_out, B1);
  not not_12 (not_12_out, B2);
  not not_13 (not_13_out, B3);
  not not_14 (not_14_out, B0);
  not not_15 (not_15_out, B1);
  not not_16 (not_16_out, B2);
  not not_17 (not_17_out, B3);
  not not_18 (not_18_out, B0);
  not not_19 (not_19_out, B1);
  not not_20 (not_20_out, B2);
  not not_21 (not_21_out, B3);
  not not_22 (not_22_out, B0);
  not not_23 (not_23_out, B1);
  not not_24 (not_24_out, B2);
  not not_25 (not_25_out, B3);
  not not_26 (not_26_out, B4);
  not not_27 (not_27_out, B6);
  not not_28 (not_28_out, B0);
  not not_29 (not_29_out, B1);
  not not_30 (not_30_out, B2);
  not not_31 (not_31_out, B3);
  not not_32 (not_32_out, B5);
  not not_33 (not_33_out, B0);
  not not_34 (not_34_out, B1);
  not not_35 (not_35_out, B2);
  not not_36 (not_36_out, B3);
  not not_37 (not_37_out, B5);
  not not_38 (not_38_out, B0);
  not not_39 (not_39_out, B1);
  not not_40 (not_40_out, B2);
  not not_41 (not_41_out, B3);
  not not_42 (not_42_out, B5);
  not not_43 (not_43_out, B0);
  not not_44 (not_44_out, B1);
  not not_45 (not_45_out, B2);
  not not_46 (not_46_out, B3);
  and and_1 (a1, not_1_out, not_2_out, not_3_out, not_4_out, not_5_out, B5, B6);
  and and_2 (and_2_out, not_6_out, not_7_out, not_8_out, not_9_out, B5, B6);
  and and_3 (and_3_out, not_10_out, not_11_out, not_12_out, not_13_out, B4, B6);
  and and_4 (and_4_out, not_14_out, not_15_out, not_16_out, not_17_out, B4, B5);
  and and_5 (a3, not_18_out, not_19_out, not_20_out, not_21_out, B4, B5);
  and and_6 (and_6_out, not_22_out, not_23_out, not_24_out, not_25_out, not_26_out, B5, not_27_out);
  and and_7 (and_7_out, not_28_out, not_29_out, not_30_out, not_31_out, B4, not_32_out);
  and and_8 (and_8_out, not_33_out, not_34_out, not_35_out, not_36_out, not_37_out, B6);
  and and_9 (and_9_out, not_38_out, not_39_out, not_40_out, not_41_out, B4, not_42_out);
  and and_10 (and_10_out, not_43_out, not_44_out, not_45_out, not_46_out, B4, B6);
  or or_1 (a2, and_2_out, and_3_out, and_4_out);
  or or_2 (a4, and_6_out, and_7_out);
  or or_3 (a5, and_8_out, and_9_out, and_10_out);

  assign a6 = 1'b0;
  assign a7 = 1'b0;
  assign a8 = 1'b0;
endmodule

module I_typr_ALU_Ctrl (
  input  B4,
  input  B3,
  input  B2,
  input  B1,
  input  B0,
  output a1,
  output a2,
  output a3,
  output a4,
  output a5,
  output a6,
  output a7,
  output a8
);

  wire and_1_out, and_2_out, not_1_out;

  and and_1 (and_1_out, B3, B1);
  or or_1 (a4, B1, B3, B4);
  and and_2 (and_2_out, B2, B0);
  not not_1 (not_1_out, B2);
  and and_3 (a8, B3, B0);
  or or_2 (a2, and_1_out, B4);
  or or_3 (a5, and_2_out, B3, B4);
  and and_4 (a6, B3, not_1_out);

  assign a1 = 1'b0;
  assign a3 = 1'b0;
  assign a7 = B1;
endmodule

module ALU_Ctrl_Unit (
  input  [4:0] Opcode,
  input  [1:0] Function,
  output [7:0] ALU_Operations
);

  wire [7:0] i_typr_alu_ctrl_1_a8, r_type_alu_ctrl_1_a8;

  I_typr_ALU_Ctrl i_typr_alu_ctrl_1 (
    .B4(Opcode[4]), .B3(Opcode[3]), .B2(Opcode[2]), .B1(Opcode[1]), .B0(Opcode[0]),
    .a1(i_typr_alu_ctrl_1_a8[7]), .a2(i_typr_alu_ctrl_1_a8[6]), .a3(i_typr_alu_ctrl_1_a8[5]),
    .a4(i_typr_alu_ctrl_1_a8[4]), .a5(i_typr_alu_ctrl_1_a8[3]), .a6(i_typr_alu_ctrl_1_a8[2]),
    .a7(i_typr_alu_ctrl_1_a8[1]), .a8(i_typr_alu_ctrl_1_a8[0]));
  R_type_ALU_Ctrl r_type_alu_ctrl_1 (
    .B0(Opcode[4]), .B1(Opcode[3]), .B2(Opcode[2]), .B3(Opcode[1]), .B4(Opcode[0]), .B5(Function[1]),
    .B6(Function[0]), .a1(r_type_alu_ctrl_1_a8[7]), .a2(r_type_alu_ctrl_1_a8[6]),
    .a3(r_type_alu_ctrl_1_a8[5]), .a4(r_type_alu_ctrl_1_a8[4]), .a5(r_type_alu_ctrl_1_a8[3]),
    .a6(r_type_alu_ctrl_1_a8[2]), .a7(r_type_alu_ctrl_1_a8[1]), .a8(r_type_alu_ctrl_1_a8[0]));
  assign ALU_Operations = i_typr_alu_ctrl_1_a8 | r_type_alu_ctrl_1_a8;  // OR_Gate or_1, 8 bits wide
endmodule
