// Logisim project BranchUnit.circ as structural Verilog: 1 circuit, main circuit BranchUnit
module BranchUnit (
  input  in_1,
  input  in_2,
  input  [2:0] in_3,
  output out_4
);

  wire not_1_out, not_2_out;

  not not_1 (not_1_out, in_1);
  not not_2 (not_2_out, in_2);
  Multiplexer #(.select(3), .enable("false")) multiplexer_1 (
    .in0(in_1), .in1(not_1_out), .in2(in_2), .in3(not_2_out), .in4(1'b0), .out(out_4), .sel(in_3));  // open: in5, in6, in7
endmodule
