// Logisim project register file.circ as structural Verilog: 1 circuit, main circuit main
module main (
  input  in_1,
  input  [2:0] RA,
  input  [2:0] RW,
  input  [2:0] RB,
  input  [15:0] BUS_W,
  input  reg_write,
  output [15:0] Bus_A,
  output [15:0] Bus_B,
  output [15:0] out_9,
  output [15:0] out_10,
  output [15:0] out_11,
  output [15:0] out_12,
  output [15:0] out_13,
  output [15:0] out_14,
  output [15:0] out_15,
  output [15:0] out_16
);

  wire and_1_out, and_2_out, and_3_out, and_4_out, and_5_out, and_6_out, and_7_out, and_8_out,
       decoder_1_out0, decoder_1_out1, decoder_1_out2, decoder_1_out3, decoder_1_out4, decoder_1_out5,
       decoder_1_out6, decoder_1_out7;

  Decoder #(.select(3), .enable("false")) decoder_1 (
    .out0(decoder_1_out0), .out1(decoder_1_out1), .out2(decoder_1_out2), .out3(decoder_1_out3),
    .out4(decoder_1_out4), .out5(decoder_1_out5), .out6(decoder_1_out6), .out7(decoder_1_out7), .sel(RW));
  and and_1 (and_1_out, decoder_1_out0, reg_write);
  and and_2 (and_2_out, decoder_1_out1, reg_write);
  and and_3 (and_3_out, decoder_1_out2, reg_write);
  and and_4 (and_4_out, decoder_1_out3, reg_write);
  and and_5 (and_5_out, decoder_1_out4, reg_write);
  and and_6 (and_6_out, decoder_1_out5, reg_write);
  and and_7 (and_7_out, decoder_1_out6, reg_write);
  and and_8 (and_8_out, decoder_1_out7, reg_write);
  Register #(.width(16)) register_1 (.D({16{1'b0}}), .en(and_1_out), .Q(out_9), .clk(in_1));  // open: clr
  Register #(.width(16)) register_2 (.D(BUS_W), .en(and_2_out), .Q(out_10), .clk(in_1));  // open: clr
  Register #(.width(16)) register_3 (.D(BUS_W), .en(and_3_out), .Q(out_11), .clk(in_1));  // open: clr
  Register #(.width(16)) register_4 (.D(BUS_W), .en(and_4_out), .Q(out_12), .clk(in_1));  // open: clr
  Register #(.width(16)) register_5 (.D(BUS_W), .en(and_5_out), .Q(out_13), .clk(in_1));  // open: clr
  Register #(.width(16)) register_6 (.D(BUS_W), .en(and_6_out), .Q(out_14), .clk(in_1));  // open: clr
  Register #(.width(16)) register_7 (.D(BUS_W), .en(and_7_out), .Q(out_15), .clk(in_1));  // open: clr
  Register #(.width(16)) register_8 (.D(BUS_W), .en(and_8_out), .Q(out_16), .clk(in_1));  // open: clr
  Multiplexer #(.select(3), .width(16), .disabled(0), .enable("false")) multiplexer_1 (
    .in0(out_9), .in1(out_10), .in2(out_11), .in3(out_12), .in4(out_13), .in5(out_14), .in6(out_15),
    .in7(out_16), .out(Bus_A), .sel(RA));
  Multiplexer #(.select(3), .width(16), .disabled(0), .enable("false")) multiplexer_2 (
    .in0(out_9), .in1(out_10), .in2(out_11), .in3(out_12), .in4(out_13), .in5(out_14), .in6(out_15),
    .in7(out_16), .out(Bus_B), .sel(RB));

  // Other names for the same wires on the sheet: R0[15:0] = out_9; R1[15:0] = out_10; R2[15:0] = out_11;
  //   R3[15:0] = out_12; R4[15:0] = out_13; R5[15:0] = out_14; R6[15:0] = out_15; R7[15:0] = out_16;
  //   regwrite = reg_write
endmodule
