// Logisim project single.circ as structural Verilog: 1 circuit, main circuit Single Cycle
module Single_Cycle (
);

  wire ALUSrc, branch, clk, Is_J_JAL, Is_JR, Mem_Read, Mem_Write, MemToReg, Reg_Write, Sign_Extend, Slt, Zero;
  wire [1:0] BUS_W, Reg_Dst;
  wire [2:0] branch_op, multiplexer_2_out;
  wire [4:0] OP;
  wire [7:0] ALUoperations;
  wire [10:0] _11_immediate;
  wire [15:0] adder_2_out, adder_3_out, alu_1_p6, bit_extender_1_out, bit_extender_2_out, bit_extender_3_out,
       I_R_Output, main_1_bus_a, main_1_bus_b, multiplexer_1_out, multiplexer_3_out, multiplexer_4_out,
       multiplexer_5_out, multiplexer_6_out, NextPC, PC, PC_1, R0, R1, R2, R3, R4, R5, R6, R7, ram_1_data;

  Register #(.width(16)) register_1 (.D(multiplexer_1_out), .Q(PC), .clk(clk));  // open: en, clr
  Multiplexer #(.width(16), .enable("false")) multiplexer_1 (
    .in0(NextPC), .in1(main_1_bus_a), .out(multiplexer_1_out), .sel(Is_JR));
  // Probe on NextPC
  Adder #(.width(16)) adder_1 (.a(16'h1), .b(PC), .out(PC_1));  // open: cin, cout
  ROM #(.addrWidth(16), .dataWidth(16)) rom_1 (.addr(PC), .data({OP, _11_immediate}));  // open: sel
  BranchUnit branchunit_1 (.in_1(Zero), .in_2(Slt), .in_3(branch_op), .out_4(branch));
  // Control_Unit control_unit_1: pin names not known; wires that end beside it: OP, _11_immediate[10:9], ALUSrc, Sign_Extend, Mem_Write, Mem_Read, MemToReg, BUS_W, Reg_Dst, Reg_Write, Is_J_JAL, branch_op, Is_JR, ALUoperations
  Multiplexer #(.select(2), .width(3), .enable("false")) multiplexer_2 (
    .in0(_11_immediate[2:0]), .in1(_11_immediate[8:6]), .in2(3'b001), .in3(3'b111), .out(multiplexer_2_out),
    .sel(Reg_Dst));
  Multiplexer #(.select(2), .width(16), .enable("false")) multiplexer_3 (
    .in0(I_R_Output), .in2({_11_immediate, {5{1'b0}}}), .in3(PC_1), .out(multiplexer_3_out), .sel(BUS_W));  // open: in1
  register_file_main main_1 (
    .RW(multiplexer_2_out), .BUS_W(multiplexer_3_out), .RA(_11_immediate[5:3]), .Bus_A(main_1_bus_a),
    .Bus_B(main_1_bus_b), .RB(_11_immediate[2:0]), .reg_write(Reg_Write), .out_9(R0), .out_10(R1),
    .out_11(R2), .out_12(R3), .out_13(R4), .out_14(R5), .out_15(R6), .out_16(R7), .in_1(clk));
  assign bit_extender_1_out = {{11{1'b0}}, _11_immediate[10:6]};  // Bit_Extender bit_extender_1
  assign bit_extender_2_out = {{11{_11_immediate[10]}}, _11_immediate[10:6]};  // Bit_Extender bit_extender_2
  assign bit_extender_3_out = {{5{_11_immediate[10]}}, _11_immediate};  // Bit_Extender bit_extender_3
  Multiplexer #(.width(16), .enable("false")) multiplexer_4 (
    .in0(bit_extender_1_out), .in1(bit_extender_2_out), .out(multiplexer_4_out), .sel(Sign_Extend));
  // Probe on PC
  // Probe on R0
  // Probe on R1
  // Probe on R2
  // Probe on R3
  // Probe on R4
  // Probe on R5
  // Probe on R6
  // Probe on R7
  Multiplexer #(.width(16), .enable("false")) multiplexer_5 (
    .in0(main_1_bus_b), .in1(multiplexer_4_out), .out(multiplexer_5_out), .sel(ALUSrc));
  Adder #(.width(16)) adder_2 (.a(PC), .b(bit_extender_3_out), .out(adder_2_out));  // open: cin, cout
  Adder #(.width(16)) adder_3 (.a(PC), .b(multiplexer_4_out), .out(adder_3_out));  // open: cin, cout
  Clock clock_1 (.out(clk));
  Multiplexer #(.width(16), .enable("false")) multiplexer_6 (
    .in0(PC_1), .in1(adder_3_out), .out(multiplexer_6_out), .sel(branch));
  Multiplexer #(.width(16), .enable("false")) multiplexer_7 (
    .in0(multiplexer_6_out), .in1(adder_2_out), .out(NextPC), .sel(Is_J_JAL));
  // ALU alu_1: pin names not known; wires that end beside it: main_1_bus_a, multiplexer_5_out, Zero, ALUoperations, Slt, alu_1_p6
  RAM #(.addrWidth(16), .dataWidth(16), .bus("separate")) ram_1 (
    .addr(alu_1_p6), .din(main_1_bus_b), .data(ram_1_data), .str(Mem_Write), .clk(clk), .ld(Mem_Read));  // open: sel, clr
  Multiplexer #(.width(16), .enable("false")) multiplexer_8 (
    .in0(alu_1_p6), .in1(ram_1_data), .out(I_R_Output), .sel(MemToReg));

  // Other names for the same wires on the sheet: upper_11_immediate[15:5] = _11_immediate;
  //   F[1:0] = _11_immediate[10:9]

  // Notes on the sheet:
  //   contents of rom_1 (hex, n*v repeats v):
  //   3883 38c3 f803 3809 39ea 3985
  //   Rs
  //   Rt
  //   Rd
  //   5_immediate
endmodule
